// Digital circuit full_adder.dig as structural Verilog
module full_adder (
  input  A,
  input  B,
  input  C_i,
  output S,
  output C_o
);

  wire and_1_out, and_2_out, xor_1_out;

  and and_1 (and_1_out, B, A);
  or or_1 (C_o, and_2_out, and_1_out);
  and and_2 (and_2_out, xor_1_out, C_i);
  xor xor_1 (xor_1_out, B, A);
  xor xor_2 (S, xor_1_out, C_i);
endmodule
