// Digital circuit logic.dig as structural Verilog
module \logic  (
  input  A,
  input  B,
  input  [1:0] S,
  output Q
);

  wire \and , \nor , \or , \xor ;

  and and_1 (\and , B, A);
  or or_1 (\or , B, A);
  Multiplexer #(.Selector_Bits(2)) multiplexer_1 (
    .sel(S), .in_0(\and ), .in_1(\or ), .in_2(\xor ), .in_3(\nor ), .out(Q));
  xor xor_1 (\xor , B, A);
  nor nor_1 (\nor , B, A);
endmodule

/* Test case:
S A B Q

# and
0 0 0 0
0 0 1 0
0 1 0 0
0 1 1 1

# or
1 0 0 0
1 0 1 1
1 1 0 1
1 1 1 1

# xor
2 0 0 0
2 0 1 1
2 1 0 1
2 1 1 0

# nor
3 0 0 1
3 0 1 0
3 1 0 0
3 1 1 0
*/
