// Digital circuit sll1.dig as structural Verilog
module sll1 (
  input  [7:0] X,
  input  S,
  output [7:0] R
);

  Multiplexer multiplexer_1 (.sel(S), .in_0(X[7]), .in_1(X[6]), .out(R[7]));
  Multiplexer multiplexer_2 (.sel(S), .in_0(X[6]), .in_1(X[5]), .out(R[6]));
  Multiplexer multiplexer_3 (.sel(S), .in_0(X[5]), .in_1(X[4]), .out(R[5]));
  Multiplexer multiplexer_4 (.sel(S), .in_0(X[4]), .in_1(X[3]), .out(R[4]));
  Multiplexer multiplexer_5 (.sel(S), .in_0(X[3]), .in_1(X[2]), .out(R[3]));
  Multiplexer multiplexer_6 (.sel(S), .in_0(X[2]), .in_1(X[1]), .out(R[2]));
  Multiplexer multiplexer_7 (.sel(S), .in_0(X[1]), .in_1(X[0]), .out(R[1]));
  Multiplexer multiplexer_8 (.sel(S), .in_0(X[0]), .in_1(1'b0), .out(R[0]));

  // Other names for the same wires on the sheet: R_0 = R[0]; R_1 = R[1]; R_2 = R[2]; R_3 = R[3]; R_4 = R[4];
  //   R_5 = R[5]; R_6 = R[6]; R_7 = R[7]; X_0 = X[0]; X_1 = X[1]; X_2 = X[2]; X_3 = X[3]; X_4 = X[4]; X_5 = X[5];
  //   X_6 = X[6]; X_7 = X[7]
endmodule

/* Test case SLL1:
# input shift result
X S R
0b11110001 0 0b11110001
0b11110001 1 0b11100010
*/
