// Digital circuit sll_any.dig as structural Verilog
module sll_any (
  input  [31:0] X,
  input  [4:0] shamt,
  output [31:0] R
);

  wire [31:0] a, a_SLL8, b, b_SLL4, c, c_SLL2, d, d_SLL1, X_SLL16;

  BarrelShifter #(.Bits(32)) SLL16 (.in(X), .shift(6'b010000), .out(X_SLL16));
  Multiplexer #(.Bits(32)) multiplexer_1 (.sel(shamt[4]), .in_0(X), .in_1(X_SLL16), .out(a));
  BarrelShifter #(.Bits(32)) SLL8 (.in(a), .shift(6'b001000), .out(a_SLL8));
  Multiplexer #(.Bits(32)) multiplexer_2 (.sel(shamt[3]), .in_0(a), .in_1(a_SLL8), .out(b));
  BarrelShifter #(.Bits(32)) SLL4 (.in(b), .shift(6'b000100), .out(b_SLL4));
  Multiplexer #(.Bits(32)) multiplexer_3 (.sel(shamt[2]), .in_0(b), .in_1(b_SLL4), .out(c));
  BarrelShifter #(.Bits(32)) SLL2 (.in(c), .shift(6'b000010), .out(c_SLL2));
  Multiplexer #(.Bits(32)) multiplexer_4 (.sel(shamt[1]), .in_0(c), .in_1(c_SLL2), .out(d));
  BarrelShifter #(.Bits(32)) SLL1 (.in(d), .shift(6'b000001), .out(d_SLL1));
  Multiplexer #(.Bits(32)) multiplexer_5 (.sel(shamt[0]), .in_0(d), .in_1(d_SLL1), .out(R));

  // Other names for the same wires on the sheet: shamt_0 = shamt[0]; shamt_1 = shamt[1]; shamt_2 = shamt[2];
  //   shamt_3 = shamt[3]; shamt_4 = shamt[4]

  // Notes on the sheet:
  //   (shift amount)
endmodule

/* Test case:
X shamt R
1 0 1
1 1 2
1 2 4
1 3 8
1 4 16
1 5 32
1 6 64
1 7 128
1 8 256
1 9 512
1 10 1024
1 11 2048
1 12 4096
1 13 8192
1 14 16384
1 15 32768
1 16 65536
1 17 131072
1 18 262144
1 19 524288
1 20 1048576
1 21 2097152
1 22 4194304
1 23 8388608
1 24 16777216
1 25 33554432
1 26 67108864
1 27 134217728
1 28 268435456
1 29 536870912
1 30 1073741824
1 31 2147483648
# overflow
0xdeadbeef 5 0xd5b7dde0
*/
