// Digital circuit sc.dig as structural Verilog
module sc (
  input  A,
  input  CLK,
  input  B,
  input  C,
  input  D,
  output Y
);

  wire register_1_q, register_2_q, register_3_q, register_4_q, xor_1_out, xor_2_out, xor_3_out;

  Register register_1 (.D(A), .C(CLK), .en(1'b1), .Q(register_1_q));
  Register register_2 (.D(B), .C(CLK), .en(1'b1), .Q(register_2_q));
  Register register_3 (.D(C), .C(CLK), .en(1'b1), .Q(register_3_q));
  Register register_4 (.D(D), .C(CLK), .en(1'b1), .Q(register_4_q));
  xor xor_1 (xor_1_out, register_1_q, register_2_q);
  xor xor_2 (xor_2_out, register_3_q, register_4_q);
  xor xor_3 (xor_3_out, xor_1_out, xor_2_out);
  Register register_5 (.D(xor_3_out), .C(CLK), .en(1'b1), .Q(Y));
endmodule

/* Test case:
CLK A B C D Y
# Y goes 1 0 1 0, 5 clock cycles required
# in steady state, one output computed per cycle
# throughput = 1 / clock period
C 1 0 0 0 0
C 0 0 0 0 1
C 1 0 0 0 0
C 0 0 0 0 1
C 1 0 0 0 0
*/
