// Digital circuit program_counter.dig as structural Verilog
module program_counter (
  input  EN,
  input  CLK,
  input  [3:0] newPC,
  input  J,
  input  CLR,
  output [3:0] PC
);

  CounterPreset #(.maxValue(15), .Bits(4)) counterpreset_1 (
    .en(EN), .C(CLK), .dir(1'b0), .in(newPC), .ld(J), .clr(CLR), .out(PC));  // open: ovf
endmodule

/* Test case:
EN CLK newPC J CLR PC
1 0 0 0 0 0
loop(n, 16)
	1 C 0 0 0 (n+1)
end loop

# J = 1
loop(n, 16)
	1 C (n) 1 0 (n)
end loop
*/
