// Digital circuit ram.dig as structural Verilog
module ram (
  input  CLK,
  input  ld,
  input  str,
  input  [7:0] Data,
  input  [3:0] Addr,
  output [7:0] out_6
);

  RAMDualPort #(.AddrBits(4), .Bits(8)) ramdualport_1 (.A(Addr), .Din(Data), .str(str), .C(CLK), .ld(ld), .D(out_6));
endmodule
