// Digital circuit rom.dig as structural Verilog
module rom (
  input  [8:0] addr,
  input  sel,
  output [15:0] out_3
);

  ROM #(.AddrBits(9), .Bits(16)) rom_1 (.A(addr), .sel(sel), .D(out_3));

  // Notes on the sheet:
  //   contents of rom_1 (hex, n*v repeats v):
  //   dead,beef,cafe,c0de,face,f00d
endmodule
