// Digital circuit tristate_buffer.dig as structural Verilog
module tristate_buffer (
  input  X,
  input  en_0,
  input  en_1,
  input  Y,
  output out
);

  assign out = en_0 ? X : 1'bz;  // Driver driver_1
  assign out = en_1 ? Y : 1'bz;  // Driver driver_2
endmodule

/* Test case:
X Y en_0 en_1 out
0 0 0 0 Z
0 0 0 1 0
0 0 1 0 0
0 0 1 1 0
0 1 0 0 Z
0 1 0 1 1
0 1 1 0 0
# 0 1 1 1 cannot enable both buffers and X != Y
1 0 0 0 Z
1 0 0 1 0
1 0 1 0 1
# 1 0 1 1 cannot enable both buffers and X != Y
1 1 0 0 Z
1 1 0 1 1
1 1 1 0 1
1 1 1 1 1
*/
